# Fritzing sketch esp32_gy30 (saved by Fritzing 0.9.3b)
breadboards: 1

parts:
  Part1 = BH1750FVI Breakout Board [part_number=BH1750FVI]
  Part2 = ESP32-DevKitC V4 by cmmc

nets:
  N1: Part1.GND, Part2.V_BATT
  VCC: Part1.VCC, Part2.3.3V

custom parts:
  BH1750FVI Breakout Board: The ROHM Semiconductor BH1750FVI is a digital ambient light sensor for the I2C bus interface. The BH750FVI is able to detect a wide range of light intensities (1-65535 lux). The spectral range is similar to that of the human eye.
